// Logisim project ALU.circ as structural Verilog: 11 circuits, main circuit Arithmetic unit
module ALU (
  input  [31:0] Rs,
  input  [31:0] Rt,
  input  [12:0] ALU_Control,
  output Overflow,
  output [31:0] ALU_Output,
  output Branch
);

  wire comparator_1_eq, comparator_1_lt, comparator_2_lt, not_1_out, not_2_out, not_3_out;
  wire [31:0] arithmetic_unit_1_arith_output, Logic_unit_logic_output, SET_unit_logic_output,
       Shift_unit_shift_output;

  Comparator #(.width(32)) comparator_1 (.a(Rs), .b(Rt), .eq(comparator_1_eq), .lt(comparator_1_lt));  // open: gt
  Comparator #(.width(32), .mode("unsigned")) comparator_2 (.a(Rs), .b(Rt), .lt(comparator_2_lt));  // open: gt, eq
  Arithmetic_unit arithmetic_unit_1 (
    .Rs(Rs), .Rt(Rt), .Arithmetic_Control(ALU_Control[2:0]), .Overflow(Overflow),
    .Arith_Output(arithmetic_unit_1_arith_output));  // open: Carryout
  Logic_unit Logic_unit (.Rs(Rs), .Rt(Rt), .Logic_Output(Logic_unit_logic_output), .Logic_Control(ALU_Control[4:3]));
  Shift_unit Shift_unit (.Rs(Rs), .Rt(Rt), .Shift_Output(Shift_unit_shift_output), .Shift_Control(ALU_Control[6:5]));
  SET_unit SET_unit (.Rs(Rs), .Rt(Rt), .Logic_Output(SET_unit_logic_output), .SET_Control(ALU_Control[7]));
  not not_1 (not_1_out, comparator_1_lt);
  not not_2 (not_2_out, comparator_2_lt);
  Multiplexer #(.select(2), .width(32), .enable("false")) multiplexer_1 (
    .in0(arithmetic_unit_1_arith_output), .in1(Logic_unit_logic_output), .in2(Shift_unit_shift_output),
    .in3(SET_unit_logic_output), .out(ALU_Output), .sel(ALU_Control[9:8]));
  not not_3 (not_3_out, comparator_1_eq);
  Multiplexer #(.select(3), .enable("false")) multiplexer_2 (
    .in0(1'b0), .in1(comparator_1_eq), .in2(not_3_out), .in3(comparator_1_lt), .in4(not_1_out),
    .in5(comparator_2_lt), .in6(not_2_out), .out(Branch), .sel(ALU_Control[12:10]));  // open: in7

  // Notes on the sheet:
  //   BLT
  //   Arithmetic unit
  //   BEQ
  //   BGE
  //   BNE
  //   BLTU
  //   BGEU
endmodule

module Arithmetic_unit (
  input  [31:0] Rs,
  input  [31:0] Rt,
  input  [2:0] Arithmetic_Control,
  output Overflow,
  output Carryout,
  output [31:0] Arith_Output
);

  wire adder_1_cout, and_1_out, and_2_out, and_3_out, and_4_out, and_5_out, and_6_out, and_7_out, and_8_out,
       and_9_out, and_10_out, comparator_1_eq, comparator_1_lt, comparator_2_lt, comparator_3_gt,
       comparator_3_lt, comparator_4_gt, comparator_4_lt, comparator_5_gt, comparator_5_lt, comparator_6_gt,
       comparator_6_lt, comparator_7_gt, comparator_7_lt, not_1_out, not_2_out, not_3_out, or_2_out,
       or_3_out, subtractor_1_bout;
  wire [31:0] ADD___ADDI, MUL, SEQ___SEQI, SLT___SLTI, SLTU___SLTIU, SUB;

  Adder #(.width(32)) adder_1 (.a(Rs), .b(Rt), .out(ADD___ADDI), .cout(adder_1_cout));  // open: cin
  Subtractor #(.width(32)) subtractor_1 (.a(Rs), .b(Rt), .out(SUB), .bout(subtractor_1_bout));  // open: bin
  Multiplier #(.width(32)) multiplier_1 (.a(Rs), .b(Rt), .out(MUL));  // open: cin, cout
  Comparator #(.width(32)) comparator_1 (.a(Rs), .b(Rt), .eq(comparator_1_eq), .lt(comparator_1_lt));  // open: gt
  Comparator #(.width(32), .mode("unsigned")) comparator_2 (.a(Rs), .b(Rt), .lt(comparator_2_lt));  // open: gt, eq
  assign SEQ___SEQI = {{31{1'b0}}, comparator_1_eq};  // Bit_Extender bit_extender_1
  assign SLT___SLTI = {{31{1'b0}}, comparator_1_lt};  // Bit_Extender bit_extender_2
  assign SLTU___SLTIU = {{31{1'b0}}, comparator_2_lt};  // Bit_Extender bit_extender_3
  // Probe on Arith_Output
  Multiplexer #(.select(3), .width(32), .enable("false")) multiplexer_1 (
    .in0(ADD___ADDI), .in1(SUB), .in2(SLT___SLTI), .in3(SLTU___SLTIU), .in4(SEQ___SEQI), .in5(MUL),
    .out(Arith_Output), .sel(Arithmetic_Control));  // open: in6, in7
  not not_1 (not_1_out, Arithmetic_Control[0]);
  not not_2 (not_2_out, Arithmetic_Control[1]);
  not not_3 (not_3_out, Arithmetic_Control[2]);
  and and_1 (and_1_out, not_1_out, not_2_out, not_3_out);
  and and_2 (and_2_out, not_1_out, Arithmetic_Control[1], not_3_out);
  Comparator #(.width(32)) comparator_3 (
    .a(Rs), .b({32{1'b0}}), .gt(comparator_3_gt), .lt(comparator_3_lt));  // open: eq
  Comparator #(.width(32)) comparator_4 (
    .a(Rt), .b({32{1'b0}}), .gt(comparator_4_gt), .lt(comparator_4_lt));  // open: eq
  Comparator #(.width(32)) comparator_5 (
    .a(ADD___ADDI), .b({32{1'b0}}), .gt(comparator_5_gt), .lt(comparator_5_lt));  // open: eq
  Comparator #(.width(32)) comparator_6 (
    .a(SUB), .b({32{1'b0}}), .gt(comparator_6_gt), .lt(comparator_6_lt));  // open: eq
  Comparator #(.width(32)) comparator_7 (.a(Rs), .b(Rt), .gt(comparator_7_gt), .lt(comparator_7_lt));  // open: eq
  and and_3 (and_3_out, comparator_3_gt, comparator_4_gt, comparator_5_lt);
  and and_4 (and_4_out, comparator_5_gt, comparator_4_lt, comparator_3_lt);
  and and_5 (and_5_out, comparator_6_lt, comparator_7_gt);
  and and_6 (and_6_out, comparator_6_gt, comparator_7_lt);
  and and_7 (and_7_out, adder_1_cout, and_1_out);
  or or_1 (Carryout, and_7_out, and_8_out);
  and and_8 (and_8_out, subtractor_1_bout, and_2_out);
  or or_2 (or_2_out, and_3_out, and_4_out);
  or or_3 (or_3_out, and_5_out, and_6_out);
  and and_9 (and_9_out, or_2_out, and_1_out);
  or or_4 (Overflow, and_9_out, and_10_out);
  and and_10 (and_10_out, or_3_out, and_2_out);
endmodule

module Logic_unit (
  input  [31:0] Rs,
  input  [31:0] Rt,
  input  [1:0] Logic_Control,
  output [31:0] Logic_Output
);

  wire [31:0] AND___ANDI, NOR___NORI, OR___ORI, XOR___XORI;

  assign AND___ANDI = Rs & Rt;  // AND_Gate AND, 32 bits wide
  assign OR___ORI = Rs | Rt;  // OR_Gate OR, 32 bits wide
  assign NOR___NORI = ~(Rs | Rt);  // NOR_Gate NOR, 32 bits wide
  assign XOR___XORI = Rs ^ Rt;  // XOR_Gate XOR, 32 bits wide
  Multiplexer #(.select(2), .width(32)) multiplexer_1 (
    .in0(XOR___XORI), .in1(OR___ORI), .in2(AND___ANDI), .in3(NOR___NORI), .out(Logic_Output),
    .sel(Logic_Control));  // open: en
endmodule

module Shift_unit (
  input  [31:0] Rs,
  input  [31:0] Rt,
  input  [1:0] Shift_Control,
  output [31:0] Shift_Output
);

  wire [31:0] ROR___RORI, SLL___SLLI, SRA___SRAI, SRL___SRLI;

  Shifter #(.width(32)) shifter_1 (.in(Rs), .\dist (Rt[4:0]), .out(SLL___SLLI));
  Shifter #(.width(32), .shift("lr")) shifter_2 (.in(Rs), .\dist (Rt[4:0]), .out(SRL___SRLI));
  Shifter #(.width(32), .shift("ar")) shifter_3 (.in(Rs), .\dist (Rt[4:0]), .out(SRA___SRAI));
  Shifter #(.width(32), .shift("rr")) shifter_4 (.in(Rs), .\dist (Rt[4:0]), .out(ROR___RORI));
  Multiplexer #(.select(2), .width(32)) multiplexer_1 (
    .in0(SLL___SLLI), .in1(SRL___SRLI), .in2(SRA___SRAI), .in3(ROR___RORI), .out(Shift_Output),
    .sel(Shift_Control));  // open: en

  // Notes on the sheet:
  //   SLL
endmodule

module SET_unit (
  input  [31:0] Rs,
  input  [31:0] Rt,
  input  SET_Control,
  output [31:0] Logic_Output
);

  wire [31:0] shifter_1_out, shifter_2_out, SSET;

  Shifter #(.width(32)) shifter_1 (.in(Rs), .\dist (5'b01111), .out(shifter_1_out));
  Multiplexer #(.width(32)) multiplexer_1 (.in0(Rt), .in1(SSET), .out(Logic_Output), .sel(SET_Control));  // open: en
  Shifter #(.width(32)) shifter_2 (.in(shifter_1_out), .\dist (5'b00001), .out(shifter_2_out));
  assign SSET = shifter_2_out | Rt;  // OR_Gate or_1, 32 bits wide

  // Other names for the same wires on the sheet: SET[31:0] = Rt
endmodule

module ALU_Control (
  input  [5:0] Opcode,
  input  [10:0] Function,
  output [12:0] ALU_Control
);

  wire and_1_out, and_2_out, and_3_out, and_4_out, and_5_out, and_6_out, and_7_out, and_8_out, and_9_out,
       and_10_out, and_11_out, and_14_out, and_15_out, and_16_out, and_17_out, and_18_out, and_19_out,
       and_20_out, and_21_out, and_22_out, and_23_out, and_24_out, and_25_out, and_26_out, and_27_out,
       and_28_out, and_29_out, and_30_out, and_31_out, and_32_out, and_33_out, and_34_out, and_35_out,
       and_36_out, and_37_out, and_38_out, and_39_out, and_40_out, and_41_out, nand_1_out, nor_1_out,
       nor_2_out, nor_3_out, nor_4_out, nor_5_out, nor_6_out, nor_7_out, nor_8_out, nor_9_out, nor_10_out,
       nor_11_out, nor_12_out, nor_13_out, nor_14_out, nor_15_out, nor_16_out, nor_17_out, nor_18_out,
       nor_19_out, nor_20_out, nor_21_out, nor_22_out, nor_23_out, nor_24_out, nor_25_out, nor_26_out,
       nor_27_out, nor_28_out, nor_29_out, nor_30_out, nor_31_out, nor_32_out, nor_33_out, nor_34_out,
       nor_35_out, nor_36_out, nor_37_out, nor_38_out, nor_39_out, not_1_out, not_2_out, SET_Operation,
       SLL_Operation, XOR_Operation;

  nand nand_1 (nand_1_out, Opcode[0], Opcode[1], Opcode[2], Opcode[3], Opcode[4], Function[1], Function[3]);
  nor nor_1 (nor_1_out, Opcode[0], Opcode[1], Opcode[2], Opcode[3], Opcode[4], Function[3]);
  nor nor_2 (nor_2_out, Opcode[0], Opcode[1], Opcode[2], Opcode[3], Opcode[4], Function[1]);
  nor nor_3 (nor_3_out, Opcode[3], Opcode[4]);
  nor nor_4 (nor_4_out, Opcode[0], Opcode[1], Opcode[2], Opcode[3], Opcode[4], Function[0], Function[3]);
  nor nor_5 (nor_5_out, Opcode[0], Opcode[1], Opcode[2], Opcode[3], Opcode[4], Function[3]);
  nor nor_6 (nor_6_out, Opcode[0], Opcode[3], Opcode[4]);
  nor nor_7 (nor_7_out, Opcode[3], Opcode[4]);
  nor nor_8 (nor_8_out, Opcode[0], Opcode[1], Opcode[2], Opcode[3], Opcode[4], Function[0], Function[1], Function[2]);
  nor nor_9 (nor_9_out, Opcode[0], Opcode[1], Opcode[2], Opcode[3], Opcode[4], Function[1]);
  nor nor_10 (nor_10_out, Opcode[0], Opcode[1], Opcode[2], Opcode[4]);
  and and_1 (and_1_out, Function[0], Function[2], nand_1_out);
  and and_2 (and_2_out, Function[0], Function[1], Function[2], nor_1_out);
  and and_3 (and_3_out, Function[0], Function[2], Function[3], nor_2_out);
  and and_4 (and_4_out, Opcode[0], Opcode[1], Opcode[2], nor_3_out);
  and and_5 (and_5_out, Function[1], Function[2], nor_4_out);
  and and_6 (and_6_out, Function[0], Function[1], Function[2], nor_5_out);
  and and_7 (and_7_out, Opcode[1], Opcode[2], nor_6_out);
  and and_8 (and_8_out, Opcode[0], Opcode[1], Opcode[2], nor_7_out);
  and and_9 (and_9_out, nor_8_out, Function[3]);
  and and_10 (and_10_out, Function[0], Function[2], Function[3], nor_9_out);
  and and_11 (and_11_out, nor_10_out, Opcode[3]);
  or or_1 (ALU_Control[0], and_1_out, and_2_out, and_3_out, and_4_out);
  or or_2 (ALU_Control[1], and_5_out, and_6_out, and_7_out, and_8_out);
  or or_3 (ALU_Control[2], and_9_out, and_10_out, and_11_out);
  nor nor_11 (nor_11_out, Opcode[0], Opcode[4]);
  nor nor_12 (nor_12_out, Opcode[1], Opcode[4]);
  nor nor_13 (nor_13_out, Opcode[0], Opcode[1], Opcode[2], Opcode[3], Opcode[4], Function[0], Function[2]);
  nor nor_14 (nor_14_out, Opcode[0], Opcode[1], Opcode[2], Opcode[3], Opcode[4], Function[0], Function[1]);
  nor nor_15 (nor_15_out, Opcode[0], Opcode[2], Opcode[4]);
  nor nor_16 (nor_16_out, Opcode[0], Opcode[1], Opcode[4]);
  nor nor_17 (nor_17_out, Opcode[0], Opcode[1], Opcode[2], Opcode[3], Opcode[4], Function[2]);
  nor nor_18 (nor_18_out, Opcode[0], Opcode[1], Opcode[2], Opcode[3], Opcode[4], Function[0], Function[1]);
  nor nor_19 (nor_19_out, Opcode[2], Opcode[4]);
  nor nor_20 (nor_20_out, Opcode[0], Opcode[1], Opcode[4]);
  and and_12 (ALU_Control[7], Opcode[1], Opcode[2], Opcode[3], nor_11_out);
  and and_13 (SET_Operation, Opcode[0], Opcode[2], Opcode[3], nor_12_out);
  and and_14 (and_14_out, Function[1], Function[3], nor_13_out);
  and and_15 (and_15_out, Function[2], Function[3], nor_14_out);
  and and_16 (and_16_out, Opcode[1], Opcode[3], nor_15_out);
  and and_17 (and_17_out, Opcode[2], Opcode[3], nor_16_out);
  and and_18 (and_18_out, Function[0], Function[1], Function[3], nor_17_out);
  and and_19 (and_19_out, Function[2], Function[3], nor_18_out);
  and and_20 (and_20_out, Opcode[0], Opcode[1], Opcode[3], nor_19_out);
  and and_21 (and_21_out, Opcode[2], Opcode[3], nor_20_out);
  or or_4 (ALU_Control[3], and_14_out, and_15_out, and_16_out, and_17_out);
  or or_5 (ALU_Control[4], and_18_out, and_19_out, and_20_out, and_21_out);
  nor nor_21 (nor_21_out, Opcode[0], Opcode[1], Opcode[2], Opcode[3], Opcode[4], Function[1], Function[2], Function[3]);
  nor nor_22 (nor_22_out, Opcode[0], Opcode[1], Opcode[2], Opcode[3], Opcode[4], Function[2], Function[3]);
  nor nor_23 (nor_23_out, Opcode[0], Opcode[2], Opcode[3], Opcode[4]);
  nor nor_24 (nor_24_out, Opcode[0], Opcode[1], Opcode[3], Opcode[4]);
  nor nor_25 (nor_25_out, Opcode[0], Opcode[1], Opcode[2], Opcode[3], Opcode[4], Function[0], Function[2], Function[3]);
  nor nor_26 (nor_26_out, Opcode[0], Opcode[1], Opcode[2], Opcode[3], Opcode[4], Function[2], Function[3]);
  nor nor_27 (nor_27_out, Opcode[2], Opcode[3], Opcode[4]);
  nor nor_28 (nor_28_out, Opcode[0], Opcode[1], Opcode[3], Opcode[4]);
  or or_6 (ALU_Control[8], ALU_Control[7], SET_Operation, XOR_Operation, ALU_Control[3], ALU_Control[4]);
  or or_7 (ALU_Control[9], ALU_Control[7], SET_Operation, SLL_Operation, ALU_Control[5], ALU_Control[6]);
  and and_22 (and_22_out, nor_21_out, Function[0]);
  and and_23 (and_23_out, Function[0], Function[1], nor_22_out);
  and and_24 (and_24_out, nor_23_out, Opcode[1]);
  and and_25 (and_25_out, nor_24_out, Opcode[2]);
  and and_26 (and_26_out, nor_25_out, Function[1]);
  and and_27 (and_27_out, Function[0], Function[1], nor_26_out);
  and and_28 (and_28_out, Opcode[0], Opcode[1], nor_27_out);
  and and_29 (and_29_out, nor_28_out, Opcode[2]);
  or or_8 (ALU_Control[5], and_22_out, and_23_out, and_24_out, and_25_out);
  or or_9 (ALU_Control[6], and_26_out, and_27_out, and_28_out, and_29_out);
  nor nor_29 (nor_29_out, Opcode[0], Opcode[2], Opcode[3]);
  nor nor_30 (nor_30_out, Opcode[0], Opcode[1], Opcode[3]);
  nor nor_31 (nor_31_out, Opcode[0], Opcode[3]);
  nor nor_32 (nor_32_out, Opcode[2], Opcode[3]);
  nor nor_33 (nor_33_out, Opcode[0], Opcode[1], Opcode[3]);
  not not_1 (not_1_out, Opcode[3]);
  nor nor_34 (nor_34_out, Opcode[1], Opcode[3]);
  nor nor_35 (nor_35_out, Opcode[0], Opcode[3]);
  not not_2 (not_2_out, Opcode[3]);
  nor nor_36 (nor_36_out, Opcode[1], Opcode[2], Opcode[3], Opcode[4]);
  nor nor_37 (nor_37_out, Opcode[0], Opcode[1], Opcode[2], Opcode[3], Opcode[4], Function[1], Function[2]);
  nor nor_38 (nor_38_out, Opcode[1], Opcode[2], Opcode[4]);
  and and_30 (and_30_out, Opcode[1], Opcode[4], nor_29_out);
  and and_31 (and_31_out, Opcode[2], Opcode[4], nor_30_out);
  and and_32 (and_32_out, Opcode[1], Opcode[2], Opcode[4], nor_31_out);
  and and_33 (and_33_out, Opcode[0], Opcode[1], Opcode[4], nor_32_out);
  and and_34 (and_34_out, Opcode[2], Opcode[4], nor_33_out);
  and and_35 (and_35_out, Opcode[0], Opcode[1], Opcode[2], Opcode[4], not_1_out);
  and and_36 (and_36_out, Opcode[0], Opcode[2], Opcode[4], nor_34_out);
  and and_37 (and_37_out, Opcode[1], Opcode[2], Opcode[4], nor_35_out);
  and and_38 (and_38_out, Opcode[0], Opcode[1], Opcode[2], Opcode[4], not_2_out);
  nor nor_39 (nor_39_out, Opcode[0], Opcode[1], Opcode[2], Opcode[3], Opcode[4], Function[0], Function[1], Function[2], Function[3]);
  or or_10 (SLL_Operation, nor_39_out, and_39_out);
  and and_39 (and_39_out, nor_36_out, Opcode[0]);
  and and_40 (and_40_out, Function[0], Function[3], nor_37_out);
  or or_11 (XOR_Operation, and_40_out, and_41_out);
  and and_41 (and_41_out, Opcode[0], Opcode[3], nor_38_out);
  or or_12 (ALU_Control[10], and_30_out, and_31_out, and_32_out);
  or or_13 (ALU_Control[11], and_33_out, and_34_out, and_35_out);
  or or_14 (ALU_Control[12], and_36_out, and_37_out, and_38_out);

  // Other names for the same wires on the sheet: Arithmetic_Control[2:0] = ALU_Control[2:0];
  //   Logic_Control[1:0] = ALU_Control[4:3]; Shift_Control[1:0] = ALU_Control[6:5]; SET_Control = ALU_Control[7];
  //   ALU_Unit_Control[1:0] = ALU_Control[9:8]; Branch_Control[2:0] = ALU_Control[12:10]; Func0 = Function[0];
  //   Func1 = Function[1]; Func2 = Function[2]; Func3 = Function[3]; Op0 = Opcode[0]; Op1 = Opcode[1];
  //   Op2 = Opcode[2]; Op3 = Opcode[3]; Op4 = Opcode[4]
endmodule

module Arithmetic_Control (
  input  [5:0] Opcode,
  input  [10:0] Function,
  output bit0,
  output bit1,
  output bit2
);

  wire and_1_out, and_2_out, and_3_out, and_4_out, and_5_out, and_6_out, and_7_out, and_8_out, and_9_out,
       and_10_out, and_11_out, nand_1_out, nor_1_out, nor_2_out, nor_3_out, nor_4_out, nor_5_out, nor_6_out,
       nor_7_out, nor_8_out, nor_9_out, nor_10_out;

  nand nand_1 (nand_1_out, Opcode[0], Opcode[1], Opcode[2], Opcode[3], Opcode[4], Function[1], Function[3]);
  nor nor_1 (nor_1_out, Opcode[0], Opcode[1], Opcode[2], Opcode[3], Opcode[4], Function[3]);
  nor nor_2 (nor_2_out, Opcode[0], Opcode[1], Opcode[2], Opcode[3], Opcode[4], Function[1]);
  nor nor_3 (nor_3_out, Opcode[3], Opcode[4]);
  nor nor_4 (nor_4_out, Opcode[0], Opcode[1], Opcode[2], Opcode[3], Opcode[4], Function[0], Function[3]);
  nor nor_5 (nor_5_out, Opcode[0], Opcode[1], Opcode[2], Opcode[3], Opcode[4], Function[3]);
  nor nor_6 (nor_6_out, Opcode[0], Opcode[3], Opcode[4]);
  nor nor_7 (nor_7_out, Opcode[3], Opcode[4]);
  nor nor_8 (nor_8_out, Opcode[0], Opcode[1], Opcode[2], Opcode[3], Opcode[4], Function[0], Function[1], Function[2]);
  nor nor_9 (nor_9_out, Opcode[0], Opcode[1], Opcode[2], Opcode[3], Opcode[4], Function[1]);
  nor nor_10 (nor_10_out, Opcode[0], Opcode[1], Opcode[2], Opcode[4]);
  and and_1 (and_1_out, Function[0], Function[2], nand_1_out);
  and and_2 (and_2_out, Function[0], Function[1], Function[2], nor_1_out);
  and and_3 (and_3_out, Function[0], Function[2], Function[3], nor_2_out);
  and and_4 (and_4_out, Opcode[0], Opcode[1], Opcode[2], nor_3_out);
  and and_5 (and_5_out, Function[1], Function[2], nor_4_out);
  and and_6 (and_6_out, Function[0], Function[1], Function[2], nor_5_out);
  and and_7 (and_7_out, Opcode[1], Opcode[2], nor_6_out);
  and and_8 (and_8_out, Opcode[0], Opcode[1], Opcode[2], nor_7_out);
  and and_9 (and_9_out, nor_8_out, Function[3]);
  and and_10 (and_10_out, Function[0], Function[2], Function[3], nor_9_out);
  and and_11 (and_11_out, nor_10_out, Opcode[3]);
  or or_1 (bit0, and_1_out, and_2_out, and_3_out, and_4_out);
  or or_2 (bit1, and_5_out, and_6_out, and_7_out, and_8_out);
  or or_3 (bit2, and_9_out, and_10_out, and_11_out);

  // Other names for the same wires on the sheet: Func0 = Function[0]; Func1 = Function[1]; Func2 = Function[2];
  //   Func3 = Function[3]; Op0 = Opcode[0]; Op1 = Opcode[1]; Op2 = Opcode[2]; Op3 = Opcode[3]; Op4 = Opcode[4]
endmodule

module Logic_Control (
  input  Op0,
  input  Op1,
  input  Op2,
  input  Op3,
  input  Op4,
  input  F0,
  input  F1,
  input  F2,
  input  F3,
  output bit0,
  output bit1
);

  wire and_1_out, and_2_out, and_3_out, and_4_out, and_5_out, and_6_out, and_7_out, and_8_out, nor_1_out,
       nor_2_out, nor_3_out, nor_4_out, nor_5_out, nor_6_out, nor_7_out, nor_8_out;

  nor nor_1 (nor_1_out, Op0, Op1, Op2, Op3, Op4, F0, F2);
  nor nor_2 (nor_2_out, Op0, Op1, Op2, Op3, Op4, F0, F1);
  nor nor_3 (nor_3_out, Op0, Op2, Op4);
  nor nor_4 (nor_4_out, Op0, Op1, Op4);
  nor nor_5 (nor_5_out, Op0, Op1, Op2, Op3, Op4, F2);
  nor nor_6 (nor_6_out, Op0, Op1, Op2, Op3, Op4, F0, F1);
  nor nor_7 (nor_7_out, Op2, Op4);
  nor nor_8 (nor_8_out, Op0, Op1, Op4);
  and and_1 (and_1_out, F1, F3, nor_1_out);
  and and_2 (and_2_out, F2, F3, nor_2_out);
  and and_3 (and_3_out, Op1, Op3, nor_3_out);
  and and_4 (and_4_out, Op2, Op3, nor_4_out);
  and and_5 (and_5_out, F0, F1, F3, nor_5_out);
  and and_6 (and_6_out, F2, F3, nor_6_out);
  and and_7 (and_7_out, Op0, Op1, Op3, nor_7_out);
  and and_8 (and_8_out, Op2, Op3, nor_8_out);
  or or_1 (bit0, and_1_out, and_2_out, and_3_out, and_4_out);
  or or_2 (bit1, and_5_out, and_6_out, and_7_out, and_8_out);
endmodule

module Shift_Control (
  input  Op0,
  input  Op1,
  input  Op2,
  input  Op3,
  input  Op4,
  input  F0,
  input  F1,
  input  F2,
  input  F3,
  output bit0,
  output bit1
);

  wire and_1_out, and_2_out, and_3_out, and_4_out, and_5_out, and_6_out, and_7_out, and_8_out, nor_1_out,
       nor_2_out, nor_3_out, nor_4_out, nor_5_out, nor_6_out, nor_7_out, nor_8_out;

  nor nor_1 (nor_1_out, Op0, Op1, Op2, Op3, Op4, F1, F2, F3);
  nor nor_2 (nor_2_out, Op0, Op1, Op2, Op3, Op4, F2, F3);
  nor nor_3 (nor_3_out, Op0, Op2, Op3, Op4);
  nor nor_4 (nor_4_out, Op0, Op1, Op3, Op4);
  nor nor_5 (nor_5_out, Op0, Op1, Op2, Op3, Op4, F0, F2, F3);
  nor nor_6 (nor_6_out, Op0, Op1, Op2, Op3, Op4, F2, F3);
  nor nor_7 (nor_7_out, Op2, Op3, Op4);
  nor nor_8 (nor_8_out, Op0, Op1, Op3, Op4);
  and and_1 (and_1_out, nor_1_out, F0);
  and and_2 (and_2_out, F0, F1, nor_2_out);
  and and_3 (and_3_out, nor_3_out, Op1);
  and and_4 (and_4_out, nor_4_out, Op2);
  and and_5 (and_5_out, nor_5_out, F1);
  and and_6 (and_6_out, F0, F1, nor_6_out);
  and and_7 (and_7_out, Op0, Op1, nor_7_out);
  and and_8 (and_8_out, nor_8_out, Op2);
  or or_1 (bit0, and_1_out, and_2_out, and_3_out, and_4_out);
  or or_2 (bit1, and_5_out, and_6_out, and_7_out, and_8_out);
endmodule

module SET_Control (
  input  [5:0] Opcode,
  output bit0,
  output bitSET
);

  wire nand_1_out, nand_2_out;

  nand nand_1 (nand_1_out, Opcode[0], Opcode[4]);
  nand nand_2 (nand_2_out, Opcode[1], Opcode[4]);
  and and_1 (bit0, Opcode[1], Opcode[2], Opcode[3], nand_1_out);
  and and_2 (bitSET, Opcode[0], Opcode[2], Opcode[3], nand_2_out);

  // Other names for the same wires on the sheet: Op0 = Opcode[0]; Op1 = Opcode[1]; Op2 = Opcode[2]; Op3 = Opcode[3];
  //   Op4 = Opcode[4]
endmodule

module Branch_Control (
  input  [5:0] Opcode,
  output bit0,
  output bit1,
  output bit2
);

  wire and_1_out, and_2_out, and_3_out, and_4_out, and_5_out, and_6_out, and_7_out, and_8_out, and_9_out,
       nor_1_out, nor_2_out, nor_3_out, nor_4_out, nor_5_out, nor_6_out, nor_7_out, not_1_out, not_2_out;

  nor nor_1 (nor_1_out, Opcode[0], Opcode[2], Opcode[3]);
  nor nor_2 (nor_2_out, Opcode[0], Opcode[1], Opcode[3]);
  nor nor_3 (nor_3_out, Opcode[0], Opcode[3]);
  nor nor_4 (nor_4_out, Opcode[2], Opcode[3]);
  nor nor_5 (nor_5_out, Opcode[0], Opcode[1], Opcode[3]);
  not not_1 (not_1_out, Opcode[3]);
  nor nor_6 (nor_6_out, Opcode[1], Opcode[3]);
  nor nor_7 (nor_7_out, Opcode[0], Opcode[3]);
  not not_2 (not_2_out, Opcode[3]);
  and and_1 (and_1_out, Opcode[1], Opcode[4], nor_1_out);
  and and_2 (and_2_out, Opcode[2], Opcode[4], nor_2_out);
  and and_3 (and_3_out, Opcode[1], Opcode[2], Opcode[4], nor_3_out);
  and and_4 (and_4_out, Opcode[0], Opcode[1], Opcode[4], nor_4_out);
  and and_5 (and_5_out, Opcode[2], Opcode[4], nor_5_out);
  and and_6 (and_6_out, Opcode[0], Opcode[1], Opcode[2], Opcode[4], not_1_out);
  and and_7 (and_7_out, Opcode[0], Opcode[2], Opcode[4], nor_6_out);
  and and_8 (and_8_out, Opcode[1], Opcode[2], Opcode[4], nor_7_out);
  and and_9 (and_9_out, Opcode[0], Opcode[1], Opcode[2], Opcode[4], not_2_out);
  or or_1 (bit0, and_1_out, and_2_out, and_3_out);
  or or_2 (bit1, and_4_out, and_5_out, and_6_out);
  or or_3 (bit2, and_7_out, and_8_out, and_9_out);

  // Other names for the same wires on the sheet: Op0 = Opcode[0]; Op1 = Opcode[1]; Op2 = Opcode[2]; Op3 = Opcode[3];
  //   Op4 = Opcode[4]
endmodule
