// Logisim project Control_Unit.circ as structural Verilog: 3 circuits, main circuit Control Signal Unit
module Control_Signal_Unit (
  input  [5:0] OP6,
  output out_2,
  output out_3,
  output out_4,
  output out_5,
  output out_6,
  output [1:0] out_7,
  output out_8,
  output out_9,
  output out_10
);

  J_Branch j_branch_1 (._6_bit_Op(OP6), .Jump(out_2));  // open: Branch
  AluSrc_Ex_Control alusrc_ex_control_1 (.Alu_Src(out_9), .ExtOp(out_8), .in_1(OP6));
  Imm_Select imm_select_1 (.Imm_Select(out_10), .in_1(OP6));
  Storage_Control_Unit storage_control_unit_1 (
    .RegSrc(out_3), .RegWr(out_4), .MemRd(out_5), .MemWr(out_6), .MemtoReg(out_7), .in_1(OP6));
endmodule

module Imm_Select (
  input  [5:0] in_1,
  output Imm_Select
);

  wire and_1_out, and_2_out, and_3_out;

  and and_1 (and_1_out, in_1[4], in_1[0]);
  and and_2 (and_2_out, in_1[4], in_1[1]);
  and and_3 (and_3_out, in_1[4], in_1[2]);
  or or_1 (Imm_Select, and_1_out, and_2_out, and_3_out);

  // Other names for the same wires on the sheet: Op0 = in_1[0]; Op1 = in_1[1]; Op2 = in_1[2]; Op3 = in_1[3];
  //   Op4 = in_1[4]; Op5 = in_1[5]
endmodule

module AluSrc_Ex_Control (
  input  [5:0] in_1,
  output Alu_Src,
  output ExtOp
);

  wire and_1_out, and_2_out, and_3_out, and_4_out, and_5_out, and_6_out, not_1_out, not_2_out, not_3_out,
       not_4_out, not_5_out, not_6_out, not_7_out;

  not not_1 (not_1_out, in_1[4]);
  not not_2 (not_2_out, in_1[4]);
  not not_3 (not_3_out, in_1[4]);
  not not_4 (not_4_out, in_1[2]);
  not not_5 (not_5_out, in_1[1]);
  not not_6 (not_6_out, in_1[2]);
  not not_7 (not_7_out, in_1[1]);
  and and_1 (and_1_out, not_1_out, in_1[0]);
  and and_2 (and_2_out, not_2_out, in_1[1]);
  and and_3 (and_3_out, not_3_out, in_1[2]);
  and and_4 (and_4_out, in_1[4], not_4_out, not_5_out);
  and and_5 (and_5_out, not_6_out, not_7_out, in_1[0]);
  or or_1 (ExtOp, and_5_out, and_6_out, in_1[4]);
  and and_6 (and_6_out, in_1[2], in_1[1]);
  or or_2 (Alu_Src, and_1_out, and_2_out, and_3_out, in_1[3], and_4_out);

  // Other names for the same wires on the sheet: Op0 = in_1[0]; Op1 = in_1[1]; Op2 = in_1[2]; Op3 = in_1[3];
  //   Op4 = in_1[4]
endmodule
