// Logisim project Instruction_Memory.circ as structural Verilog: 1 circuit, main circuit Instruction Memory
module Instruction_Memory (
  input  [19:0] PC,
  output [31:0] _32_bit_iinstruction
);

  ROM #(.addrWidth(20), .dataWidth(32)) rom_1 (.addr(PC), .data(_32_bit_iinstruction));  // open: sel

  // Notes on the sheet:
  //   INSTRUCTION MEMORY
  //   contents of rom_1 (hex, n*v repeats v):
  //   1100011
endmodule
