// Logisim project Pipeline_Processor.circ as structural Verilog: 6 circuits, main circuit Pipline_Processor
module Pipline_Processor (
);

  wire alu_1_p5, ALUSrc, B, button_1_out, clock_1_out, Ext, ImmSelect, J, MemRd, MemWr, RegSource, RegWr;
  wire [1:0] MemtoReg;
  wire [4:0] ImmL, instruction_spliter_1_rd, instruction_spliter_1_rs1, instruction_spliter_1_rs2,
       multiplexer_3_out;
  wire [5:0] OpCode;
  wire [10:0] Function, ImmU;
  wire [12:0] alu_control_1_alu_control;
  wire [15:0] Imm16;
  wire [19:0] BranshPC, JumpPC, multiplexer_1_out, PC, PC_1;
  wire [31:0] ALUOut, data_memory_1_data_out, Ext_PC, Extended, instruction_memory_1__32_bit_iinstruction,
       multiplexer_2_out, multiplexer_4_out, Output, R0, R1, R2, R3, R4, R5, R6, R7, R8, R9, R10, R11, R12,
       R13, R14, R15, R16, R17, R18, R19, R20, R21, R22, R23, R24, R25, R26, R27, R28, R29, R30, R31, Rs1,
       Rs2;

  Multiplexer #(.select(2), .width(20), .enable("false")) multiplexer_1 (
    .in0(PC_1), .in1(BranshPC), .in2(JumpPC), .in3({20{1'b0}}), .out(multiplexer_1_out), .sel({J, B}));
  Jump jump_1 (.Imm16(Imm16), .Pc_jump(JumpPC), .Rs1(Rs1));
  Register #(.width(20)) Register (.D(multiplexer_1_out), .en(1'b1), .Q(PC), .clk(clock_1_out), .clr(button_1_out));
  Button button_1 (.out(button_1_out));
  PC_1 pc_1_1 (.Initial_Pc(PC), .OutPcPlus1(PC_1));
  Control_Signal_Unit control_signal_unit_1 (
    .OP6(OpCode), .out_2(J), .out_4(RegWr), .out_5(MemRd), .out_6(MemWr), .out_7(MemtoReg), .out_8(Ext),
    .out_9(ALUSrc), .out_10(ImmSelect), .out_3(RegSource));
  Branch_pc branch_pc_1 (.ImmL(ImmL), .ImmU(ImmU), .initial_pc(PC), .Pc_Branch(BranshPC));
  Instruction_Memory instruction_memory_1 (.PC(PC), ._32_bit_iinstruction(instruction_memory_1__32_bit_iinstruction));
  Multiplexer #(.width(32), .enable("false")) multiplexer_2 (
    .in0(instruction_memory_1__32_bit_iinstruction), .out(multiplexer_2_out));  // open: in1, sel
  // Probe on R0
  // Probe on R1
  // Probe on R2
  // Probe on R3
  // Probe on R4
  // Probe on R5
  // Probe on R6
  // Probe on R7
  Instruction_Spliter instruction_spliter_1 (
    .in_1(multiplexer_2_out), .Opcode(OpCode), .RD(instruction_spliter_1_rd), .ImmL(ImmL),
    .Rs1(instruction_spliter_1_rs1), .Rs2(instruction_spliter_1_rs2), .ImmU(ImmU), .F(Function),
    .Imm16(Imm16), .CLK(clock_1_out));
  Multiplexer #(.width(5), .enable("false")) multiplexer_3 (
    .in0(instruction_spliter_1_rs1), .in1(instruction_spliter_1_rd), .out(multiplexer_3_out), .sel(RegSource));
  // Probe on R8
  // Probe on R9
  // Probe on R10
  // Probe on R11
  // Probe on R12
  // Probe on R13
  // Probe on R14
  // Probe on R15
  // Probe on B
  Clock clock_1 (.out(clock_1_out));
  // Probe on R16
  // Probe on R17
  // Probe on R18
  // Probe on R19
  // Probe on R20
  // Probe on R21
  // Probe on R22
  // Probe on R23
  // Probe on PC
  Register_File register_file_1 (
    .BusW(Output), .RegWrite(RegWr), .R2(R2), .R3(R3), .R4(R4), .R5(R5), .R6(R6), .R7(R7), .R8(R8), .R9(R9),
    .R10(R10), .R11(R11), .R12(R12), .R14(R14), .R15(R15), .R16(R16), .R17(R17), .R18(R18), .R19(R19),
    .R20(R20), .R21(R21), .R22(R22), .R23(R23), .R24(R24), .R25(R25), .R26(R26), .R27(R27), .R28(R28),
    .R29(R29), .R30(R30), .R31(R31), .BusA(Rs1), .BusB(Rs2), .R1(R1), .R13(R13), .Rs1(multiplexer_3_out),
    .Rs2(instruction_spliter_1_rs2), .Clock(clock_1_out), .Rd(instruction_spliter_1_rd), .R0(R0));
  // Probe on J
  // Probe on R24
  // Probe on R25
  // Probe on R26
  // Probe on R27
  // Probe on R28
  // Probe on R29
  // Probe on R30
  // Probe on R31
  Multiplexer #(.width(32), .enable("false")) multiplexer_4 (
    .in0(Rs2), .in1(Extended), .out(multiplexer_4_out), .sel(ALUSrc));
  ALU_Control alu_control_1 (.ALU_Control(alu_control_1_alu_control), .Opcode(OpCode), .Function(Function));
  // ALU alu_1: pin names not known; wires that end beside it: Rs1, multiplexer_4_out, B, alu_control_1_alu_control, alu_1_p5, alu_1_p5, ALUOut
  Extender extender_1 (
    .Extender_Op(Ext), .Immediate(Extended), .Imm16(Imm16), .ImmSelect(ImmSelect), .ImmU(ImmU), .ImmL(ImmL),
    .PC_1(PC_1), .PC_Extended(Ext_PC));
  Data_Memory data_memory_1 (
    .Address(ALUOut), .Data_In(Rs2), .Memory_Write(MemWr), .Clock(clock_1_out),
    .Data_Out(data_memory_1_data_out), .Memory_Read(MemRd));
  Multiplexer #(.select(2), .width(32), .enable("false")) multiplexer_5 (
    .in0(ALUOut), .in1(data_memory_1_data_out), .in2(Ext_PC), .out(Output), .sel(MemtoReg));  // open: in3
endmodule

module Instruction_Spliter (
  input  [31:0] in_1,
  input  CLK,
  output [5:0] Opcode,
  output [4:0] RD,
  output [4:0] ImmL,
  output [4:0] Rs1,
  output [15:0] Imm16,
  output [10:0] F,
  output [10:0] ImmU,
  output [4:0] Rs2
);

  Register #(.width(32)) Instrucrion_Register (
    .D(in_1), .en(1'b1), .Q({F, Imm16[4:0], Rs1, ImmL, Opcode}), .clk(CLK));  // open: clr

  assign Imm16[15:5] = F;
  assign ImmU = F;
  assign RD = ImmL;
  assign Rs2 = Imm16[4:0];

  // Notes on the sheet:
  //   SB_Type
  //   R_Tube
  //   I-Type
endmodule

module IF_ID_Registers (
  input  [19:0] Pc_1,
  input  [31:0] in_2,
  input  CLK,
  output [19:0] out_4,
  output [31:0] out_5
);

  Register #(.width(20)) Next_PC (.D(Pc_1), .en(1'b1), .Q(out_4), .clk(CLK));  // open: clr
  Register #(.width(32)) Instruction_Word (.D(in_2), .en(1'b1), .Q(out_5), .clk(CLK));  // open: clr
endmodule

module ID_Ex (
  input  [19:0] in_1,
  input  in_2,
  input  [15:0] in_3,
  input  [12:0] in_4,
  input  [31:0] in_5,
  input  in_6,
  input  [31:0] in_7,
  input  in_8,
  input  [31:0] in_9,
  input  [1:0] in_10,
  input  in_11,
  output [19:0] out_12,
  output out_13,
  output [15:0] out_14,
  output [12:0] out_15,
  output [31:0] out_16,
  output out_17,
  output [31:0] out_18,
  output out_19,
  output [31:0] out_20,
  output [1:0] out_21
);

  Register #(.width(20)) Next_PC (.D(in_1), .en(1'b1), .Q(out_12), .clk(in_11));  // open: clr
  Register #(.width(16)) Imm16 (.D(in_3), .en(1'b1), .Q(out_14), .clk(in_11));  // open: clr
  Register #(.width(32)) BusA (.D(in_5), .en(1'b1), .Q(out_16), .clk(in_11));  // open: clr
  Register #(.width(32)) BusB (.D(in_7), .en(1'b1), .Q(out_18), .clk(in_11));  // open: clr
  Register #(.width(32)) Rd (.D(in_9), .en(1'b1), .Q(out_20), .clk(in_11));  // open: clr
  Register #(.width(1)) Alu_Src (.D(in_2), .en(1'b1), .Q(out_13), .clk(in_11));  // open: clr
  Register #(.width(13)) Alu_Control (.D(in_4), .en(1'b1), .Q(out_15), .clk(in_11));  // open: clr
  Register #(.width(1)) MemRd (.D(in_6), .en(1'b1), .Q(out_17), .clk(in_11));  // open: clr
  Register #(.width(1)) MemWr (.D(in_8), .en(1'b1), .Q(out_19), .clk(in_11));  // open: clr
  Register #(.width(2)) MemtoReg (.D(in_10), .en(1'b1), .Q(out_21), .clk(in_11));  // open: clr

  // Notes on the sheet:
  //   Signals
endmodule

module Ex_MEM (
  input  [31:0] in_1,
  input  in_2,
  input  [31:0] in_3,
  input  in_4,
  input  [1:0] in_5,
  input  [31:0] in_6,
  input  in_7,
  output [31:0] out_8,
  output out_9,
  output [31:0] out_10,
  output out_11,
  output [1:0] out_12,
  output [31:0] out_13
);

  Register #(.width(32)) Alu_Out (.D(in_1), .en(1'b1), .Q(out_8), .clk(in_7));  // open: clr
  Register #(.width(32)) Rt (.D(in_3), .en(1'b1), .Q(out_10), .clk(in_7));  // open: clr
  Register #(.width(32)) Rd (.D(in_6), .en(1'b1), .Q(out_13), .clk(in_7));  // open: clr
  Register #(.width(1)) MemRd (.D(in_2), .en(1'b1), .Q(out_9), .clk(in_7));  // open: clr
  Register #(.width(1)) MemWr (.D(in_4), .en(1'b1), .Q(out_11), .clk(in_7));  // open: clr
  Register #(.width(2)) MemToReg (.D(in_5), .en(1'b1), .Q(out_12), .clk(in_7));  // open: clr

  // Notes on the sheet:
  //   Signals
endmodule

module MEM_WB (
  input  [31:0] in_1,
  input  [1:0] in_2,
  input  CLk,
  input  [31:0] in_4,
  output [31:0] out_5,
  output [1:0] out_6,
  output [31:0] out_7
);

  Register #(.width(32)) WB (.D(in_1), .en(1'b1), .Q(out_5), .clk(CLk));  // open: clr
  Register #(.width(32)) Rd (.D(in_4), .en(1'b1), .Q(out_7), .clk(CLk));  // open: clr
  Register #(.width(2)) MemToReg (.D(in_2), .en(1'b1), .Q(out_6), .clk(CLk));  // open: clr

  // Notes on the sheet:
  //   Signals
endmodule
